// Logisim project u16a.circ as structural Verilog: 1 circuit, main circuit main
module main (
);

  wire ADDR_WRITE, ALU_F, ALU_NO, ALU_NX, ALU_NY, ALU_OUT_NEG, ALU_OUT_ZERO, ALU_READ, ALU_ZX, ALU_ZY,
       and_1_out, and_2_out, and_3_out, and_4_out, and_5_out, and_6_out, and_7_out, BX_READ, BX_WRITE,
       BY_READ, BY_WRITE, CLK, decoder_1_out6, decoder_1_out7, decoder_2_out7, demultiplexer_1_out0,
       demultiplexer_1_out1, INST_STEP_RESET, INST_WRITE, INV_CLK, IP_COUNT, IP_READ, IP_WRITE, not_2_out,
       RAM_READ, RAM_WRITE;
  wire [2:0] INST_STEP_q;
  wire [3:0] ADDR_q;
  wire [11:0] INST_q;
  wire [13:0] MICROINSTRUCTIONS_data;
  wire [14:0] multiplexer_6_out;
  wire [15:0] adder_1_out, ALU_IN_X, ALU_IN_Y, and_8_out, DBUS, dipswitch_1_sw16, IP_q, multiplexer_1_out,
       multiplexer_2_out, multiplexer_3_out, multiplexer_4_out, multiplexer_5_out, not_3_out, not_4_out,
       not_5_out, ram_1_dout, register_1_q, register_2_q;
  wire [15:4] ADDR_q_2;

  Counter #(.max('h7), .width(3)) INST_STEP (
    .clr(INST_STEP_RESET), .load(1'b0), .up(1'b1), .count(1'b1), .clk(INV_CLK), .Q(INST_STEP_q));  // open: D, carry
  Clock clock_1 (.out(CLK));
  not not_1 (INV_CLK, CLK);
  Counter #(.max('hffff), .width(16)) IP (
    .clr(1'b0), .load(IP_WRITE), .up(1'b1), .count(IP_COUNT), .clk(CLK), .D(DBUS), .Q(IP_q));  // open: carry
  Register #(.width(16)) BX (.D(DBUS), .en(BX_WRITE), .clk(CLK), .Q(ALU_IN_X));  // open: clr
  Register #(.width(16)) BY (.D(DBUS), .en(BY_WRITE), .clk(CLK), .Q(ALU_IN_Y));  // open: clr
  Register #(.width(12)) INST (.D(DBUS[11:0]), .en(INST_WRITE), .clk(CLK), .Q(INST_q));  // open: clr
  assign DBUS = BX_READ ? ALU_IN_X : 16'bz;  // Controlled_Buffer controlled_buffer_1
  assign DBUS = BY_READ ? ALU_IN_Y : 16'bz;  // Controlled_Buffer controlled_buffer_2
  ROM #(.addrWidth(16), .dataWidth(16)) MICROINSTRUCTIONS (
    .addr({INST_q, INST_STEP_q, ALU_OUT_ZERO}),
    .data({INST_STEP_RESET, IP_COUNT, MICROINSTRUCTIONS_data[13:8], ALU_NO, ALU_F, ALU_NY, ALU_ZY, ALU_NX, ALU_ZX, MICROINSTRUCTIONS_data[1:0]}));
  assign DBUS = IP_READ ? IP_q : 16'bz;  // Controlled_Buffer controlled_buffer_3
  // Probe on {INST_STEP_RESET, IP_COUNT, MICROINSTRUCTIONS_data[13:8], ALU_NO, ALU_F, ALU_NY, ALU_ZY, ALU_NX, ALU_ZX, MICROINSTRUCTIONS_data[1:0]}
  Register #(.width(16)) ADDR (.D(DBUS), .en(ADDR_WRITE), .clk(CLK), .Q({ADDR_q_2, ADDR_q}));  // open: clr
  and and_1 (and_1_out, and_3_out, demultiplexer_1_out0);
  and and_2 (and_2_out, and_3_out, demultiplexer_1_out1);
  Demultiplexer #(.select(4)) demultiplexer_1 (
    .out0(demultiplexer_1_out0), .out1(demultiplexer_1_out1), .in(1'b1), .sel(ADDR_q));  // open: out2, out3, out4, out5, out6, out7, out8, out9, out10, out11, out12, out13, out14, out15
  Decoder #(.enable("false"), .select(3)) decoder_1 (
    .out1(RAM_READ), .out2(IP_READ), .out3(BX_READ), .out4(BY_READ), .out5(ALU_READ), .out6(decoder_1_out6),
    .out7(decoder_1_out7), .sel(MICROINSTRUCTIONS_data[10:8]));  // open: out0
  and and_3 (and_3_out, ADDR_q_2[15], ADDR_q_2[14], ADDR_q_2[13], ADDR_q_2[12]);
  DipSwitch #(.number(16)) dipswitch_1 (
    .sw1(dipswitch_1_sw16[15]), .sw2(dipswitch_1_sw16[14]), .sw3(dipswitch_1_sw16[13]),
    .sw4(dipswitch_1_sw16[12]), .sw5(dipswitch_1_sw16[11]), .sw6(dipswitch_1_sw16[10]),
    .sw7(dipswitch_1_sw16[9]), .sw8(dipswitch_1_sw16[8]), .sw9(dipswitch_1_sw16[7]),
    .sw10(dipswitch_1_sw16[6]), .sw11(dipswitch_1_sw16[5]), .sw12(dipswitch_1_sw16[4]),
    .sw13(dipswitch_1_sw16[3]), .sw14(dipswitch_1_sw16[2]), .sw15(dipswitch_1_sw16[1]),
    .sw16(dipswitch_1_sw16[0]));
  and and_4 (and_4_out, RAM_WRITE, not_2_out);
  not not_2 (not_2_out, and_3_out);
  Decoder #(.enable("false"), .select(3)) decoder_2 (
    .out1(ADDR_WRITE), .out2(INST_WRITE), .out3(IP_WRITE), .out4(BX_WRITE), .out5(BY_WRITE),
    .out6(RAM_WRITE), .out7(decoder_2_out7), .sel(MICROINSTRUCTIONS_data[13:11]));  // open: out0
  RAM #(.addrWidth(16), .asyncread("true"), .dataWidth(16), .\type ("nonvolatile")) ram_1 (
    .addr({ADDR_q_2, ADDR_q}), .we(and_4_out), .oe(1'b1), .clk(CLK), .din(DBUS), .dout(ram_1_dout));
  and and_5 (and_5_out, RAM_WRITE, and_1_out);
  Register #(.width(16)) register_1 (.D(DBUS), .en(and_5_out), .clk(CLK), .Q(register_1_q));  // open: clr
  Register #(.width(16)) register_2 (.D(dipswitch_1_sw16), .en(1'b1), .clk(CLK), .Q(register_2_q));  // open: clr
  Multiplexer #(.width(16)) multiplexer_1 (.in0(ALU_IN_X), .in1({16{1'b0}}), .out(multiplexer_1_out), .sel(ALU_ZX));
  Multiplexer #(.width(16)) multiplexer_2 (.in0(ALU_IN_Y), .in1({16{1'b0}}), .out(multiplexer_2_out), .sel(ALU_ZY));
  Multiplexer #(.width(16)) multiplexer_3 (
    .in0(multiplexer_1_out), .in1(not_3_out), .out(multiplexer_3_out), .sel(ALU_NX));
  assign not_3_out = ~multiplexer_1_out;  // NOT_Gate not_3, 16 bits wide
  Multiplexer #(.width(16)) multiplexer_4 (
    .in0(multiplexer_2_out), .in1(not_4_out), .out(multiplexer_4_out), .sel(ALU_NY));
  assign not_4_out = ~multiplexer_2_out;  // NOT_Gate not_4, 16 bits wide
  and and_6 (and_6_out, RAM_READ, not_2_out);
  and and_7 (and_7_out, RAM_READ, and_2_out);
  assign DBUS = and_7_out ? register_2_q : 16'bz;  // Controlled_Buffer controlled_buffer_4
  assign and_8_out = multiplexer_3_out & multiplexer_4_out;  // AND_Gate and_8, 16 bits wide
  Adder #(.width(16)) adder_1 (
    .a(multiplexer_3_out), .b(multiplexer_4_out), .out(adder_1_out), .cin(1'b0));  // open: cout
  assign DBUS = and_6_out ? ram_1_dout : 16'bz;  // Controlled_Buffer controlled_buffer_5
  Multiplexer #(.width(16)) multiplexer_5 (.in0(and_8_out), .in1(adder_1_out), .out(multiplexer_5_out), .sel(ALU_F));
  assign not_5_out = ~multiplexer_5_out;  // NOT_Gate not_5, 16 bits wide
  Multiplexer #(.width(16)) multiplexer_6 (
    .in0(multiplexer_5_out), .in1(not_5_out), .out({ALU_OUT_NEG, multiplexer_6_out}), .sel(ALU_NO));
  assign DBUS = ALU_READ ? {ALU_OUT_NEG, multiplexer_6_out} : 16'bz;  // Controlled_Buffer controlled_buffer_6
  nor nor_1 (ALU_OUT_ZERO, multiplexer_6_out[0], multiplexer_6_out[1], multiplexer_6_out[2], multiplexer_6_out[3], multiplexer_6_out[4], multiplexer_6_out[5], multiplexer_6_out[6], multiplexer_6_out[7], multiplexer_6_out[8], multiplexer_6_out[9], multiplexer_6_out[10], multiplexer_6_out[11], multiplexer_6_out[12], multiplexer_6_out[13], multiplexer_6_out[14], ALU_OUT_NEG);
  Hex_Digit_Display hex_digit_display_1 (.value(register_1_q[15:12]));  // open: dp
  Hex_Digit_Display hex_digit_display_2 (.value(register_1_q[11:8]));  // open: dp
  Hex_Digit_Display hex_digit_display_3 (.value(register_1_q[7:4]));  // open: dp
  Hex_Digit_Display hex_digit_display_4 (.value(register_1_q[3:0]));  // open: dp

  // Notes on the sheet:
  //   contents of MICROINSTRUCTIONS (hex, n*v repeats v):
  //   a00 a00 5100 5100 8000 8000 10*0 a00 a00 5100 5100 a00 a00 5900 5900 8000 8000 6*0 a00 a00 5100 5100
  //   25f8 25f8 8000 8000 8*0 a00 a00 5100 5100 2570 2570 8000 8000 8*0 a00 a00 5100 5100 a00 a00 6100
  //   6100 8000 8000 6*0 a00 a00 5100 5100 a00 a00 4900 4900 3300 3300 8000 8000 4*0 a00 a00 5100 5100 a00
  //   a00 4900 4900 2100 2100 8000 8000 4*0 a00 a00 5100 5100 a30 a30 4030 5930 8000 8000 6*0 a00 a00 5100
  //   5100 25ec 25ec 8000 8000 8*0 a00 a00 5100 5100 254c 254c 8000 8000 8*0 a00 a00 5100 5100 a00 a00
  //   6100 6100 8000 8000 6*0 a00 a00 5100 5100 a00 a00 4900 4900 3400 3400 8000 8000 4*0 a00 a00 5100
  //   5100 a00 a00 4900 4900 2900 2900 8000 8000 4*0 a00 a00 5100 5100 a0c a0c 400c 590c 8000 8000
endmodule
